// Digital circuit Controle ULA Simplified.dig as structural Verilog
module Controle_ULA_Simplified (
  input  [2:0] Funct,
  input  [1:0] ALUOp,
  output [2:0] ULACtrl
);

  Multiplexer #(.Selector_Bits(2), .Bits(3)) multiplexer_1 (
    .sel(ALUOp), .in_0(3'b000), .in_1(3'b101), .in_2(Funct), .in_3(3'b000), .out(ULACtrl));
endmodule
