// Digital circuit Controler.dig as structural Verilog
module Controler (
  input  CLK,
  input  in_2,
  input  in_3,
  input  in_4
);

  wire and_1_out, and_2_out, and_3_out, and_4_out, nand_1_out, nand_2_out, nand_3_out, nand_4_out,
       nand_5_out, nand_6_out, nand_7_out, nand_8_out, nand_9_out, nand_10_out, nand_11_out, nand_12_out,
       nand_13_out, nand_14_out, nand_15_out, nand_16_out, nand_17_out, nand_18_out, nand_19_out,
       nand_20_out, nand_21_out, nand_22_out, nand_23_out, nand_24_out, nand_25_out, nand_26_out,
       nand_27_out, nand_28_out, nand_29_out, nand_30_out, nand_31_out, nand_32_out, nand_33_out,
       nand_34_out, nand_35_out, nand_36_out, nand_37_out, nand_38_out, nand_39_out, nand_40_out,
       nand_41_out, nand_42_out, nand_43_out, nand_44_out, nand_45_out, nand_46_out, nand_47_out,
       nand_48_out, nand_50_out, nand_52_out, nand_54_out, nand_56_out, nand_58_out, nand_60_out,
       nand_62_out, nand_64_out, not_1_out, not_2_out, not_3_out, not_4_out, not_5_out, not_6_out, not_7_out,
       not_8_out, not_9_out, not_10_out, not_11_out, not_12_out, not_13_out, not_14_out, not_15_out,
       not_16_out, not_17_out, not_18_out, not_19_out, not_20_out, not_21_out, not_22_out, not_23_out,
       not_24_out, not_25_out, xor_1_out, xor_2_out, xor_3_out, xor_4_out, xor_5_out;
  wire [7:0] eeprom_1_d, nand_55_out;

  nand nand_1 (nand_1_out, CLK, nand_55_out[0]);
  not not_1 (not_1_out, nand_55_out[0]);
  nand nand_2 (nand_2_out, CLK, not_1_out);
  nand nand_3 (nand_3_out, CLK, nand_55_out[1]);
  not not_2 (not_2_out, nand_55_out[1]);
  nand nand_4 (nand_4_out, CLK, not_2_out);
  nand nand_5 (nand_5_out, CLK, not_25_out);
  not not_3 (not_3_out, not_25_out);
  nand nand_6 (nand_6_out, CLK, not_3_out);
  nand nand_7 (nand_7_out, CLK, xor_1_out);
  not not_4 (not_4_out, xor_1_out);
  nand nand_8 (nand_8_out, CLK, not_4_out);
  nand nand_9 (nand_9_out, CLK, xor_2_out);
  not not_5 (not_5_out, xor_2_out);
  nand nand_10 (nand_10_out, CLK, not_5_out);
  nand nand_11 (nand_11_out, CLK, xor_3_out);
  not not_6 (not_6_out, xor_3_out);
  nand nand_12 (nand_12_out, CLK, not_6_out);
  nand nand_13 (nand_13_out, CLK, xor_4_out);
  not not_7 (not_7_out, xor_4_out);
  nand nand_14 (nand_14_out, CLK, not_7_out);
  nand nand_15 (nand_15_out, CLK, xor_5_out);
  not not_8 (not_8_out, xor_5_out);
  nand nand_16 (nand_16_out, CLK, not_8_out);
  nand nand_17 (nand_17_out, nand_1_out, nand_18_out);
  nand nand_18 (nand_18_out, nand_2_out, nand_17_out);
  nand nand_19 (nand_19_out, nand_3_out, nand_20_out);
  nand nand_20 (nand_20_out, nand_4_out, nand_19_out);
  nand nand_21 (nand_21_out, nand_5_out, nand_22_out);
  nand nand_22 (nand_22_out, nand_6_out, nand_21_out);
  nand nand_23 (nand_23_out, nand_7_out, nand_24_out);
  nand nand_24 (nand_24_out, nand_8_out, nand_23_out);
  nand nand_25 (nand_25_out, nand_9_out, nand_26_out);
  nand nand_26 (nand_26_out, nand_10_out, nand_25_out);
  nand nand_27 (nand_27_out, nand_11_out, nand_28_out);
  nand nand_28 (nand_28_out, nand_12_out, nand_27_out);
  nand nand_29 (nand_29_out, nand_13_out, nand_30_out);
  nand nand_30 (nand_30_out, nand_14_out, nand_29_out);
  nand nand_31 (nand_31_out, nand_15_out, nand_32_out);
  nand nand_32 (nand_32_out, nand_16_out, nand_31_out);
  nand nand_33 (nand_33_out, not_9_out, nand_17_out);
  not not_9 (not_9_out, CLK);
  not not_10 (not_10_out, nand_17_out);
  nand nand_34 (nand_34_out, not_9_out, not_10_out);
  nand nand_35 (nand_35_out, not_11_out, nand_19_out);
  not not_11 (not_11_out, CLK);
  not not_12 (not_12_out, nand_19_out);
  nand nand_36 (nand_36_out, not_11_out, not_12_out);
  nand nand_37 (nand_37_out, not_13_out, nand_21_out);
  not not_13 (not_13_out, CLK);
  not not_14 (not_14_out, nand_21_out);
  nand nand_38 (nand_38_out, not_13_out, not_14_out);
  nand nand_39 (nand_39_out, not_15_out, nand_23_out);
  not not_15 (not_15_out, CLK);
  not not_16 (not_16_out, nand_23_out);
  nand nand_40 (nand_40_out, not_15_out, not_16_out);
  nand nand_41 (nand_41_out, not_17_out, nand_25_out);
  not not_17 (not_17_out, CLK);
  not not_18 (not_18_out, nand_25_out);
  nand nand_42 (nand_42_out, not_17_out, not_18_out);
  nand nand_43 (nand_43_out, not_19_out, nand_27_out);
  not not_19 (not_19_out, CLK);
  not not_20 (not_20_out, nand_27_out);
  nand nand_44 (nand_44_out, not_19_out, not_20_out);
  nand nand_45 (nand_45_out, not_21_out, nand_29_out);
  not not_21 (not_21_out, CLK);
  not not_22 (not_22_out, nand_29_out);
  nand nand_46 (nand_46_out, not_21_out, not_22_out);
  nand nand_47 (nand_47_out, not_23_out, nand_31_out);
  not not_23 (not_23_out, CLK);
  not not_24 (not_24_out, nand_31_out);
  nand nand_48 (nand_48_out, not_23_out, not_24_out);
  nand nand_49 (nand_55_out[0], nand_33_out, nand_50_out);
  nand nand_50 (nand_50_out, nand_34_out, nand_55_out[0]);
  nand nand_51 (nand_55_out[1], nand_35_out, nand_52_out);
  nand nand_52 (nand_52_out, nand_36_out, nand_55_out[1]);
  nand nand_53 (nand_55_out[2], nand_37_out, nand_54_out);
  nand nand_54 (nand_54_out, nand_38_out, nand_55_out[2]);
  nand nand_55 (nand_55_out[3], nand_39_out, nand_56_out);
  nand nand_56 (nand_56_out, nand_40_out, nand_55_out[3]);
  nand nand_57 (nand_55_out[4], nand_41_out, nand_58_out);
  nand nand_58 (nand_58_out, nand_42_out, nand_55_out[4]);
  nand nand_59 (nand_55_out[5], nand_43_out, nand_60_out);
  nand nand_60 (nand_60_out, nand_44_out, nand_55_out[5]);
  nand nand_61 (nand_55_out[6], nand_45_out, nand_62_out);
  nand nand_62 (nand_62_out, nand_46_out, nand_55_out[6]);
  nand nand_63 (nand_55_out[7], nand_47_out, nand_64_out);
  nand nand_64 (nand_64_out, nand_48_out, nand_55_out[7]);
  not not_25 (not_25_out, nand_55_out[2]);
  xor xor_1 (xor_1_out, nand_55_out[2], nand_55_out[3]);
  and and_1 (and_1_out, nand_55_out[3], nand_55_out[2]);
  xor xor_2 (xor_2_out, and_1_out, nand_55_out[4]);
  and and_2 (and_2_out, nand_55_out[4], and_1_out);
  xor xor_3 (xor_3_out, and_2_out, nand_55_out[5]);
  and and_3 (and_3_out, nand_55_out[5], and_2_out);
  xor xor_4 (xor_4_out, and_3_out, nand_55_out[6]);
  and and_4 (and_4_out, nand_55_out[6], and_3_out);
  xor xor_5 (xor_5_out, and_4_out, nand_55_out[7]);
  // Probe on nand_55_out
  EEPROM #(.AddrBits(8), .isProgramMemory("true"), .Bits(8)) eeprom_1 (
    .A(nand_55_out), .CS(in_2), .WE(in_3), .OE(in_4), .D(eeprom_1_d));
  // Probe on eeprom_1_d

  // Notes on the sheet:
  //   contents of eeprom_1 (hex, n*v repeats v):
  //   0,1,2,3,4,5,6,7,8,9,a,b,c,d,e,f,0,1,2,3,4,5,6,7,8,9,a,b,c,d,e
  //   ,f,0,1,2,3,4,5,6,7,8,9,a,b,c,d,e,f,0,1,2,3,4,5,6,7,8,9,a,b,c,d
  //   ,e,f,0,1,2,3,4,5,6,7,8,9,a,b,c,d,e,f,0,1,2,3,4,5,6,7,8,9,a,b,c
  //   ,d,e,f,0,1,2,3,4,5,6,7,8,9,a,b,c,d,e,f,0,1,2,3,4,5,6,7,8,9,a,b
  //   ,c,d,e,f,0,1,2,3,4,5,6,7,8,9,a,b,c,d,e,f,0,1,2,3,4,5,6,7,8,9,a
  //   ,b,c,d,e,f,0,1,2,3,4,5,6,7,8,9,a,b,c,d,e,f,0,1,2,3,4,5,6,7,8,9
  //   ,a,b,c,d,e,f,0,1,2,3,4,5,6,7,8,9,a,b,c,d,e,f,0,1,2,3,4,5,6,7,8
  //   ,9,a,b,c,d,e,f,0,1,2,3,4,5,6,7,8,9,a,b,c,d,e,f,0,1,2,3,4,5,6,7
  //   ,8,9,a,b,c,d,e,f
endmodule
