// Digital circuit Divisor.dig as structural Verilog
module Divisor (
);

  wire and_1_out, and_2_out, and_3_out, and_4_out, and_5_out, and_6_out, and_7_out, and_8_out, and_9_out,
       and_10_out, and_11_out, and_12_out, not_1_out, not_2_out, not_3_out, not_4_out, not_5_out, not_6_out,
       or_1_out, or_2_out, or_3_out, or_4_out, or_5_out, or_6_out, undriven, undriven_2, undriven_3,
       undriven_4, xor_1_out, xor_2_out, xor_3_out, xor_4_out, xor_5_out, xor_6_out;

  and and_1 (and_1_out, undriven_2, not_1_out);
  // Not not_1 has open pins: in=open, out=not_1_out
  and and_2 (and_2_out, xor_1_out, or_3_out);
  or or_1 (or_1_out, and_2_out, and_1_out);
  not not_2 (not_2_out, undriven);
  and and_3 (and_3_out, xor_2_out, not_2_out);
  xor xor_1 (xor_1_out, undriven_2, not_1_out);
  xor xor_2 (xor_2_out, or_3_out, xor_1_out);
  and and_4 (and_4_out, undriven_2, undriven);
  or or_2 (or_2_out, and_4_out, and_3_out);
  and and_5 (and_5_out, undriven_3, not_3_out);
  or or_3 (or_3_out, and_6_out, and_5_out);
  // Not not_3 has open pins: in=open, out=not_3_out
  xor xor_3 (xor_3_out, undriven_3, not_3_out);
  and and_6 (and_6_out, xor_3_out, or_5_out);
  not not_4 (not_4_out, undriven);
  and and_7 (and_7_out, xor_4_out, not_4_out);
  or or_4 (or_4_out, and_8_out, and_7_out);
  xor xor_4 (xor_4_out, or_5_out, xor_3_out);
  and and_8 (and_8_out, undriven_3, undriven);
  and and_9 (and_9_out, undriven_4, not_5_out);
  or or_5 (or_5_out, and_10_out, and_9_out);
  // Not not_5 has open pins: in=open, out=not_5_out
  xor xor_5 (xor_5_out, undriven_4, not_5_out);
  and and_10 (and_10_out, xor_5_out, 1'b1);
  not not_6 (not_6_out, undriven);
  and and_11 (and_11_out, xor_6_out, not_6_out);
  or or_6 (or_6_out, and_12_out, and_11_out);
  xor xor_6 (xor_6_out, 1'b1, xor_5_out);
  and and_12 (and_12_out, undriven_4, undriven);
endmodule
