// Digital circuit RegisterFile.dig as structural Verilog
module RegisterFile (
  input  D0
);

  wire driver_1_out, nand_1_out, nand_2_out, nand_3_out, nand_4_out, nand_5_out, nand_6_out, nand_7_out,
       nand_8_out, not_1_out, not_2_out, not_3_out, undriven, undriven_2;

  not not_1 (not_1_out, D0);
  nand nand_1 (nand_1_out, driver_1_out, D0);
  nand nand_2 (nand_2_out, driver_1_out, not_1_out);
  assign driver_1_out = undriven ? undriven_2 : 1'bz;  // Driver driver_1
  nand nand_3 (nand_3_out, nand_1_out, nand_4_out);
  nand nand_4 (nand_4_out, nand_2_out, nand_3_out);
  not not_2 (not_2_out, driver_1_out);
  not not_3 (not_3_out, nand_3_out);
  nand nand_5 (nand_5_out, not_2_out, nand_3_out);
  nand nand_6 (nand_6_out, not_2_out, not_3_out);
  nand nand_7 (nand_7_out, nand_5_out, nand_8_out);
  nand nand_8 (nand_8_out, nand_6_out, nand_7_out);
endmodule
